// Logisim project cpu.circ as structural Verilog: 4 circuits, main circuit main
module main (
  input  [15:0] From_Instr_Mem,
  input  clk,
  output [15:0] r0,
  output [15:0] r1,
  output [15:0] r2,
  output [15:0] r3,
  output [15:0] Display_0,
  output [15:0] Display_1,
  output [15:0] To_Instr_Mem,
  output [15:0] Data_Mem_Data,
  output [15:0] Data_Mem_Addr,
  output Data_Mem_Write
);

  wire ALU_equal, ALU_signed_overflow, ALUScr, beq, bne, Branch, demultiplexer_2_out0, demultiplexer_2_out1,
       display, ExtOp, j_jal, jal, jr, jump, lui, MemRead, MemtoReg, multiplexer_6_out, not_1_out, not_2_out,
       or_2_out, RegDst, RegWrt;
  wire [1:0] ALUCtr, decode_1_rd, decode_1_rs, decode_1_rt, multiplexer_3_out, multiplexer_4_out;
  wire [3:0] ALUcontrol_alu_selection, opcode;
  wire [5:0] func;
  wire [7:0] decode_1_immediate;
  wire [11:0] target_address;
  wire [15:0] adder_1_out, adder_2_out, ALU_result, and_1_out, bit_extender_1_out, bit_extender_2_out,
       bit_extender_3_out, bit_extender_4_out, demultiplexer_1_out0, demultiplexer_1_out1, multiplexer_1_out,
       multiplexer_2_out, multiplexer_5_out, multiplexer_7_out, multiplexer_8_out, multiplexer_9_out,
       multiplexer_11_out, or_3_out, RegFile_read_data_2, register_1_q, rs, shifter_1_out, WrtData;

  Control Control (
    .opcode(opcode), .RegDst(RegDst), .RegWrt(RegWrt), .Signed(ExtOp), .ALUSrc(ALUScr), .ALUOp(ALUCtr),
    .MemtoReg(MemtoReg), .MemWrt(Data_Mem_Write), .MemRead(MemRead), .Branch(Branch), .lui(lui),
    .display(display), .bne(bne), .jr(jr), .j(jump), .jar(jal));
  or or_1 (j_jal, jump, jal);
  Multiplexer #(.width(16), .enable("false")) multiplexer_1 (
    .in0(From_Instr_Mem), .in1({16{1'b0}}), .out(multiplexer_1_out), .sel(or_2_out));
  or or_2 (or_2_out, j_jal, jr, beq);
  Register #(.width(16)) PC (.D(multiplexer_9_out), .Q(To_Instr_Mem), .clk(clk));  // open: en, clr
  Register #(.width(16)) register_1 (.D(multiplexer_1_out), .Q(register_1_q), .clk(clk));  // open: en, clr
  decode decode_1 (
    .instruction(register_1_q), .target_address(target_address), .funct(func), .rs(decode_1_rs),
    .rt(decode_1_rt), .rd(decode_1_rd), .opcode(opcode), .immediate(decode_1_immediate));
  Adder #(.width(16)) adder_1 (.a(16'h1), .b(To_Instr_Mem), .out(adder_1_out));  // open: cin, cout
  assign bit_extender_1_out = {{8{1'b0}}, decode_1_immediate};  // Bit_Extender bit_extender_1
  Multiplexer #(.width(16), .enable("false")) multiplexer_2 (
    .in0(bit_extender_1_out), .in1(bit_extender_2_out), .out(multiplexer_2_out), .sel(ExtOp));
  assign bit_extender_2_out = {{8{decode_1_immediate[7]}}, decode_1_immediate};  // Bit_Extender bit_extender_2
  assign bit_extender_3_out = {{8{1'b0}}, decode_1_immediate};  // Bit_Extender bit_extender_3
  assign bit_extender_4_out = {{4{1'b0}}, target_address};  // Bit_Extender bit_extender_4
  assign and_1_out = 16'hf000 & adder_1_out;  // AND_Gate and_1, 16 bits wide
  Multiplexer #(.width(2), .enable("false")) multiplexer_3 (
    .in0(decode_1_rt), .in1(decode_1_rd), .out(multiplexer_3_out), .sel(RegDst));
  Shifter #(.width(16)) shifter_1 (.in(bit_extender_3_out), .\dist (4'b1000), .out(shifter_1_out));
  Demultiplexer #(.width(16)) demultiplexer_1 (
    .out0(demultiplexer_1_out0), .out1(demultiplexer_1_out1), .in(rs), .sel(decode_1_immediate[0]),
    .en(display));
  assign or_3_out = bit_extender_4_out | and_1_out;  // OR_Gate or_3, 16 bits wide
  Adder #(.width(16)) adder_2 (.a(To_Instr_Mem), .b(bit_extender_2_out), .out(adder_2_out));  // open: cin, cout
  Multiplexer #(.width(2), .enable("false")) multiplexer_4 (
    .in0(multiplexer_3_out), .in1(2'b11), .out(multiplexer_4_out), .sel(jal));
  Demultiplexer demultiplexer_2 (
    .out0(demultiplexer_2_out0), .out1(demultiplexer_2_out1), .in(1'b1), .sel(decode_1_immediate[0]),
    .en(display));
  Regfile_main RegFile (
    .Read_register_1(decode_1_rs), .Read_register_2(decode_1_rt), .write_register(multiplexer_4_out),
    .write_data(WrtData), .Reg_0_Value(r0), .Reg_1_Value(r1), .Reg_2_Value(r2), .Reg_3_Value(r3),
    .RegWrite(RegWrt), .clock(clk), .Read_Data_1(rs), .Read_Data_2(RegFile_read_data_2));
  Register #(.width(16)) register_2 (
    .D(demultiplexer_1_out0), .en(demultiplexer_2_out0), .Q(Display_0), .clk(clk));  // open: clr
  Register #(.width(16)) register_3 (
    .D(demultiplexer_1_out1), .en(demultiplexer_2_out1), .Q(Display_1), .clk(clk));  // open: clr
  Multiplexer #(.width(16), .enable("false")) multiplexer_5 (
    .in0(adder_1_out), .in1(adder_2_out), .out(multiplexer_5_out), .sel(beq));
  and and_2 (beq, Branch, multiplexer_6_out);
  Multiplexer #(.enable("false")) multiplexer_6 (.in0(ALU_equal), .in1(not_1_out), .out(multiplexer_6_out), .sel(bne));
  not not_1 (not_1_out, ALU_equal);
  alu_main ALU (
    .switch__S(ALUcontrol_alu_selection), .X(rs), .equal(ALU_equal), .result(ALU_result),
    .signed_overflow(ALU_signed_overflow), .Y(multiplexer_7_out));
  Multiplexer #(.width(16), .enable("false")) multiplexer_7 (
    .in0(RegFile_read_data_2), .in1(multiplexer_2_out), .out(multiplexer_7_out), .sel(ALUScr));
  ALUcontrol ALUcontrol (.ALUOp(ALUCtr), .funct(func), .ALU_selection(ALUcontrol_alu_selection));
  Multiplexer #(.width(16), .enable("false")) multiplexer_8 (
    .in0(multiplexer_5_out), .in1(or_3_out), .out(multiplexer_8_out), .sel(j_jal));
  Multiplexer #(.width(16), .enable("false")) multiplexer_9 (
    .in0(multiplexer_8_out), .in1(rs), .out(multiplexer_9_out), .sel(jr));
  LED Overflow (.in(ALU_signed_overflow));
  Multiplexer #(.width(16), .enable("false")) multiplexer_10 (
    .in0(ALU_result), .in1(shifter_1_out), .out(Data_Mem_Addr), .sel(lui));
  // _7_Segment_Display 7_segment_display_1: pin names not known; wires that end beside it: Display_0[15:12], Display_0[15:12]
  // BlockBottom blockbottom_1: pin names not known
  // BlockTop blocktop_1: pin names not known
  // _7_Segment_Display 7_segment_display_2: pin names not known; wires that end beside it: Display_0[15:12], Display_0[15:12], Display_0[11:8], Display_0[11:8], Display_0[7:4], Display_0[7:4], Display_0[3:0], Display_0[3:0]
  // _7_Segment_Display 7_segment_display_3: pin names not known; wires that end beside it: Display_0[15:12], Display_0[15:12], Display_0[11:8], Display_0[11:8], Display_0[7:4], Display_0[7:4], Display_0[3:0], Display_0[3:0]
  assign Data_Mem_Data = Data_Mem_Write ? RegFile_read_data_2 : 16'bz;  // Controlled_Buffer controlled_buffer_1
  not not_2 (not_2_out, Data_Mem_Write);
  // _7_Segment_Display 7_segment_display_4: pin names not known; wires that end beside it: Display_0[3:0], Display_0[3:0]
  RAM #(.addrWidth(16), .dataWidth(16)) ram_1 (
    .addr(Data_Mem_Addr), .data(Data_Mem_Data), .sel(1'b1), .clk(clk), .ld(not_2_out));  // open: clr
  // _7_Segment_Display 7_segment_display_5: pin names not known; wires that end beside it: Display_1[15:12], Display_1[15:12], Display_1[11:8], Display_1[11:8], Display_1[7:4], Display_1[7:4], Display_1[3:0], Display_1[3:0]
  // _7_Segment_Display 7_segment_display_6: pin names not known; wires that end beside it: Display_1[15:12], Display_1[15:12]
  // BlockBottom blockbottom_2: pin names not known
  Multiplexer #(.width(16), .enable("false")) multiplexer_11 (
    .in0(Data_Mem_Addr), .in1(Data_Mem_Data), .out(multiplexer_11_out), .sel(MemtoReg));
  Multiplexer #(.width(16), .enable("false")) multiplexer_12 (
    .in0(multiplexer_11_out), .in1(To_Instr_Mem), .out(WrtData), .sel(jal));
  // BlockTop blocktop_2: pin names not known
  // _7_Segment_Display 7_segment_display_7: pin names not known; wires that end beside it: Display_1[3:0], Display_1[3:0]
  // _7_Segment_Display 7_segment_display_8: pin names not known; wires that end beside it: Display_1[15:12], Display_1[15:12], Display_1[11:8], Display_1[11:8], Display_1[7:4], Display_1[7:4], Display_1[3:0], Display_1[3:0]

  // Other names for the same wires on the sheet: clock = clk; d0[15:0] = Display_0; d1[15:0] = Display_1;
  //   MemWrt = Data_Mem_Write; n_PC[15:0] = To_Instr_Mem

  // Notes on the sheet:
  //   "kill" instruction
  //   n_PC
  //   lui
  //   display
  //   $rt
  //   $rd
  //   PC+1
  //   $rs
  //   extended imm
  //   jump
  //   branch
  //   jr
  //   equal
  //   DISPLAY[0]
  //   DISPLAY[1]
endmodule

module decode (
  input  [15:0] instruction,
  output [11:0] target_address,
  output [5:0] funct,
  output [1:0] rs,
  output [1:0] rt,
  output [1:0] rd,
  output [3:0] opcode,
  output [7:0] immediate
);


  assign funct = instruction[5:0];
  assign immediate = instruction[7:0];
  assign opcode = instruction[15:12];
  assign rd = instruction[7:6];
  assign rs = instruction[11:10];
  assign rt = instruction[9:8];
  assign target_address = instruction[11:0];
endmodule

module ALUcontrol (
  input  [1:0] ALUOp,
  input  [5:0] funct,
  output [3:0] ALU_selection
);

  Multiplexer #(.select(2), .width(4)) multiplexer_1 (
    .in0(4'b0000), .in1(4'b0001), .in2(4'b0010), .in3(funct[3:0]), .out(ALU_selection), .sel(ALUOp));  // open: en

  // Notes on the sheet:
  //   or
  //   and
  //   add
endmodule

module Control (
  input  [3:0] opcode,
  output RegDst,
  output RegWrt,
  output Signed,
  output ALUSrc,
  output [1:0] ALUOp,
  output MemtoReg,
  output MemWrt,
  output MemRead,
  output Branch,
  output lui,
  output display,
  output bne,
  output jr,
  output j,
  output jar
);

  Multiplexer #(.select(4), .width(16)) multiplexer_1 (
    .in0(16'h33), .in1(16'h800), .in2(16'h402), .in3(16'ha), .in4(16'h1e), .in5(16'h2a), .in6(16'h8002),
    .in7(16'h4000), .in8(16'h2000), .in9(16'h204), .in10(16'h1204), .in11(16'h15e), .in12(16'h9c),
    .in13({16{1'b0}}), .in14({16{1'b0}}), .in15({16{1'b0}}),
    .out({jar, j, jr, bne, display, lui, Branch, MemRead, MemWrt, MemtoReg, ALUOp[0], ALUOp[1], ALUSrc, Signed, RegWrt, RegDst}),
    .sel(opcode));  // open: en
endmodule
