// Logisim project Regfile.circ as structural Verilog: 1 circuit, main circuit main
module main (
  input  [1:0] Read_register_1,
  input  [1:0] Read_register_2,
  input  [1:0] write_register,
  input  [15:0] write_data,
  input  RegWrite,
  input  clock,
  output [15:0] Reg_0_Value,
  output [15:0] Reg_1_Value,
  output [15:0] Reg_2_Value,
  output [15:0] Reg_3_Value,
  output [15:0] Read_Data_1,
  output [15:0] Read_Data_2
);

  wire [15:0] multiplexer_1_out, multiplexer_2_out, multiplexer_3_out, multiplexer_4_out;

  Multiplexer #(.select(2), .width(16)) multiplexer_1 (
    .in0(write_data), .in1(Reg_0_Value), .in2(Reg_0_Value), .in3(Reg_0_Value), .out(multiplexer_1_out),
    .sel(write_register));  // open: en
  Register #(.width(16)) Reg0 (.D(multiplexer_1_out), .en(RegWrite), .Q(Reg_0_Value), .clk(clock));  // open: clr
  Multiplexer #(.select(2), .width(16)) multiplexer_2 (
    .in0(Reg_1_Value), .in1(write_data), .in2(Reg_1_Value), .in3(Reg_1_Value), .out(multiplexer_2_out),
    .sel(write_register));  // open: en
  Register #(.width(16)) Reg1 (.D(multiplexer_2_out), .en(RegWrite), .Q(Reg_1_Value), .clk(clock));  // open: clr
  Multiplexer #(.select(2), .width(16)) multiplexer_3 (
    .in0(Reg_2_Value), .in1(Reg_2_Value), .in2(write_data), .in3(Reg_2_Value), .out(multiplexer_3_out),
    .sel(write_register));  // open: en
  Register #(.width(16)) Reg2 (.D(multiplexer_3_out), .en(RegWrite), .Q(Reg_2_Value), .clk(clock));  // open: clr
  Multiplexer #(.select(2), .width(16)) multiplexer_4 (
    .in0(Reg_3_Value), .in1(Reg_3_Value), .in2(Reg_3_Value), .in3(write_data), .out(multiplexer_4_out),
    .sel(write_register));  // open: en
  Register #(.width(16)) Reg3 (.D(multiplexer_4_out), .en(RegWrite), .Q(Reg_3_Value), .clk(clock));  // open: clr
  Multiplexer #(.select(2), .width(16), .enable("false")) multiplexer_5 (
    .in0(Reg_0_Value), .in1(Reg_1_Value), .in2(Reg_2_Value), .in3(Reg_3_Value), .out(Read_Data_1),
    .sel(Read_register_1));
  Multiplexer #(.select(2), .width(16), .enable("false")) multiplexer_6 (
    .in0(Reg_0_Value), .in1(Reg_1_Value), .in2(Reg_2_Value), .in3(Reg_3_Value), .out(Read_Data_2),
    .sel(Read_register_2));
endmodule
