// Logisim project alu.circ as structural Verilog: 1 circuit, main circuit main
module main (
  input  [15:0] X,
  input  [15:0] Y,
  input  [3:0] switch__S,
  output signed_overflow,
  output [15:0] result,
  output equal
);

  alu alu_1 (
    .inputA(X), .inputB(Y), .Control_Bits(switch__S), .\output (result), .Signed_Overflow(signed_overflow),
    .equal_signal(equal));  // open: Unsigned_Overflow
endmodule
