// Logisim project alu_lab.circ as structural Verilog: 18 circuits, main circuit alu
module NAND (
  input  in_1,
  input  in_2,
  output out_3
);

  wire and_1_out;

  and and_1 (and_1_out, in_1, in_2);
  not not_1 (out_3, and_1_out);
endmodule

module NOR (
  input  in_1,
  input  in_2,
  output out_3
);

  wire or_1_out;

  not not_1 (out_3, or_1_out);
  or or_1 (or_1_out, in_1, in_2);
endmodule

module XOR (
  input  in_1,
  input  in_2,
  output out_3
);

  wire and_1_out, and_2_out, not_1_out, not_2_out;

  not not_1 (not_1_out, in_2);
  not not_2 (not_2_out, in_1);
  and and_1 (and_1_out, in_1, not_1_out);
  and and_2 (and_2_out, not_2_out, in_2);
  or or_1 (out_3, and_1_out, and_2_out);
endmodule

// 2-1 MUX
module _2_TO_1_MUX (
  input  input1,
  input  input2,
  input  s,
  output \output 
);

  wire and_1_out, and_2_out, not_1_out;

  not not_1 (not_1_out, s);
  and and_1 (and_1_out, input1, not_1_out);
  and and_2 (and_2_out, s, input2);
  or or_1 (\output , and_1_out, and_2_out);
endmodule

module _4_TO_1_MUX (
  input  [15:0] INPUT1,
  input  [15:0] INPUT2,
  input  [15:0] INPUT3,
  input  [15:0] INPUT4,
  input  s0,
  input  s1,
  output [15:0] OUTPUT
);

  wire not_1_out, not_2_out;
  wire [15:0] and_1_out, and_2_out, and_3_out, and_4_out, bit_extender_1_out, bit_extender_2_out,
       bit_extender_3_out, bit_extender_4_out;

  assign bit_extender_1_out = {{15{s0}}, s0};  // Bit_Extender bit_extender_1
  assign bit_extender_2_out = {{15{not_1_out}}, not_1_out};  // Bit_Extender bit_extender_2
  not not_1 (not_1_out, s0);
  assign bit_extender_3_out = {{15{s1}}, s1};  // Bit_Extender bit_extender_3
  assign bit_extender_4_out = {{15{not_2_out}}, not_2_out};  // Bit_Extender bit_extender_4
  not not_2 (not_2_out, s1);
  assign and_1_out = INPUT1 & bit_extender_2_out & bit_extender_4_out;  // AND_Gate and_1, 16 bits wide
  assign and_2_out = INPUT2 & bit_extender_2_out & bit_extender_3_out;  // AND_Gate and_2, 16 bits wide
  assign and_3_out = INPUT3 & bit_extender_1_out & bit_extender_4_out;  // AND_Gate and_3, 16 bits wide
  assign and_4_out = INPUT4 & bit_extender_1_out & bit_extender_3_out;  // AND_Gate and_4, 16 bits wide
  assign OUTPUT = and_1_out | and_2_out | and_3_out | and_4_out;  // OR_Gate or_1, 16 bits wide
endmodule

module AddMachine (
  output [7:0] out_1,
  output [7:0] out_2
);

  wire clock_1_out;

  Adder adder_1 (.a(8'h1), .b(out_2), .out(out_1));  // open: cin, cout
  Register register_1 (.D(out_1), .Q(out_2), .clk(clock_1_out));  // open: en, clr
  Clock clock_1 (.out(clock_1_out));
endmodule

module alu (
  input  [15:0] inputA,
  input  [15:0] inputB,
  input  [3:0] Control_Bits,
  output [15:0] \output ,
  output Unsigned_Overflow,
  output Signed_Overflow,
  output equal_signal
);

  wire ADD_signed_overflow, ADD_unsigned_overflow, addp8_signed_overflow, addp8_unsigned_overflow,
       comparator_1_lt, SUB_signed_overflow, subp8_signed_overflow;
  wire [3:0] shrink_to_4_bit_1__4_bit_output, shrink_to_4_bit_2__4_bit_output,
       shrink_to_4_bit_3__4_bit_output;
  wire [15:0] ADD_output, addp8_out_3, AND_out, bit_extender_1_out, OR_out, shifter_1_out, shifter_2_out,
       shifter_3_out, sltp8_out_3, SUB_output, subp8_out_3;

  shrink_to_4_bit shrink_to_4_bit_1 (._16_bit_input(inputB), ._4_bit_output(shrink_to_4_bit_1__4_bit_output));
  shrink_to_4_bit shrink_to_4_bit_2 (._16_bit_input(inputB), ._4_bit_output(shrink_to_4_bit_2__4_bit_output));
  shrink_to_4_bit shrink_to_4_bit_3 (._16_bit_input(inputB), ._4_bit_output(shrink_to_4_bit_3__4_bit_output));
  assign OR_out = inputA | inputB;  // OR_Gate OR, 16 bits wide
  assign AND_out = inputA & inputB;  // AND_Gate AND, 16 bits wide
  ADD_16bit ADD (
    .input1(inputA), .input2(inputB), .Unsigned_Overflow(ADD_unsigned_overflow),
    .Signed_Overflow(ADD_signed_overflow), .\output (ADD_output));
  SUB_16bit SUB (.input1(inputA), .input2(inputB), .Signed_Overflow(SUB_signed_overflow), .\output (SUB_output));
  Shifter #(.width(16)) shifter_1 (.in(inputA), .\dist (shrink_to_4_bit_1__4_bit_output), .out(shifter_1_out));
  Shifter #(.width(16), .shift("lr")) shifter_2 (
    .in(inputA), .\dist (shrink_to_4_bit_2__4_bit_output), .out(shifter_2_out));
  Shifter #(.width(16), .shift("ar")) shifter_3 (
    .in(inputA), .\dist (shrink_to_4_bit_3__4_bit_output), .out(shifter_3_out));
  Comparator #(.width(16)) comparator_1 (.a(inputA), .b(inputB), .eq(equal_signal), .lt(comparator_1_lt));  // open: gt
  addp8 addp8 (
    .A(inputA), .B(inputB), .Unsigned_Overflow(addp8_unsigned_overflow),
    .Signed_Overflow(addp8_signed_overflow), .out_3(addp8_out_3));
  subp8 subp8 (.A(inputA), .B(inputB), .Signed_Overflow(subp8_signed_overflow), .out_3(subp8_out_3));
  sltp8 sltp8 (.A(inputA), .B(inputB), .out_3(sltp8_out_3));
  assign bit_extender_1_out = {{15{1'b0}}, comparator_1_lt};  // Bit_Extender bit_extender_1
  Multiplexer #(.select(4), .width(16), .enable("false")) multiplexer_1 (
    .in0(OR_out), .in1(AND_out), .in2(ADD_output), .in3(SUB_output), .in4(shifter_1_out),
    .in5(shifter_2_out), .in6(shifter_3_out), .in7(bit_extender_1_out), .in8(addp8_out_3), .in9(subp8_out_3),
    .in10(sltp8_out_3), .in11({16{1'b0}}), .in12({16{1'b0}}), .in13({16{1'b0}}), .in14({16{1'b0}}),
    .in15({16{1'b0}}), .out(\output ), .sel(Control_Bits));
  Multiplexer #(.select(4), .enable("false")) multiplexer_2 (
    .in0(1'b0), .in1(1'b0), .in2(ADD_unsigned_overflow), .in3(1'b0), .in4(1'b0), .in5(1'b0), .in6(1'b0),
    .in7(1'b0), .in8(addp8_unsigned_overflow), .in9(1'b0), .in10(1'b0), .in11(1'b0), .in12(1'b0),
    .in13(1'b0), .in14(1'b0), .in15(1'b0), .out(Unsigned_Overflow), .sel(Control_Bits));
  Multiplexer #(.select(4), .enable("false")) multiplexer_3 (
    .in0(1'b0), .in1(1'b0), .in2(ADD_signed_overflow), .in3(SUB_signed_overflow), .in4(1'b0), .in5(1'b0),
    .in6(1'b0), .in7(1'b0), .in8(addp8_signed_overflow), .in9(subp8_signed_overflow), .in10(1'b0),
    .in11(1'b0), .in12(1'b0), .in13(1'b0), .in14(1'b0), .in15(1'b0), .out(Signed_Overflow), .sel(Control_Bits));
endmodule

module _0_7_fibonacci_sequence (
  input  input1,
  input  input2,
  input  input3,
  input  input1_2,
  input  input2_2,
  input  input3_2,
  output \output ,
  output output_2
);

  wire and_1_out, and_2_out, and_3_out, and_4_out, not_1_out, not_2_out, or_1_out, or_2_out;

  and and_1 (and_1_out, input1_2, input2_2, input3_2);
  not not_1 (not_1_out, input3_2);
  and and_2 (and_2_out, input2, input3);
  not not_2 (not_2_out, input3);
  and and_3 (and_3_out, not_1_out, input1_2);
  or or_1 (or_1_out, and_2_out, not_2_out);
  or or_2 (or_2_out, and_1_out, and_3_out);
  not not_3 (output_2, or_2_out);
  and and_4 (and_4_out, input1, or_1_out);
  not not_4 (\output , and_4_out);
endmodule

module _16_to_1_MUX (
  input  [15:0] input0,
  input  [15:0] input1,
  input  [15:0] input2,
  input  [15:0] input3,
  input  [15:0] input4,
  input  [15:0] input5,
  input  [15:0] input6,
  input  [15:0] input7,
  input  [15:0] input8,
  input  [15:0] input9,
  input  [15:0] input10,
  input  [15:0] input11,
  input  [15:0] input12,
  input  [15:0] input13,
  input  [15:0] input14,
  input  [15:0] input15,
  input  s3,
  input  s2,
  input  s1,
  input  s0,
  output [15:0] \output 
);

  wire [15:0] n4_to_1_mux_1_output, n4_to_1_mux_2_output, n4_to_1_mux_3_output, n4_to_1_mux_4_output;

  _4_TO_1_MUX u_4_to_1_mux_1 (
    .INPUT1(input0), .INPUT2(input1), .INPUT3(input2), .INPUT4(input3), .s0(s1), .s1(s0),
    .OUTPUT(n4_to_1_mux_1_output));
  _4_TO_1_MUX u_4_to_1_mux_2 (
    .INPUT1(input4), .INPUT2(input5), .INPUT3(input6), .INPUT4(input7), .s0(s1), .s1(s0),
    .OUTPUT(n4_to_1_mux_2_output));
  _4_TO_1_MUX u_4_to_1_mux_3 (
    .INPUT1(input8), .INPUT2(input9), .INPUT3(input10), .INPUT4(input11), .s0(s1), .s1(s0),
    .OUTPUT(n4_to_1_mux_3_output));
  _4_TO_1_MUX u_4_to_1_mux_4 (
    .INPUT1(input12), .INPUT2(input13), .INPUT3(input14), .INPUT4(input15), .s0(s1), .s1(s0),
    .OUTPUT(n4_to_1_mux_4_output));
  _4_TO_1_MUX u_4_to_1_mux_5 (
    .INPUT1(n4_to_1_mux_1_output), .INPUT2(n4_to_1_mux_2_output), .INPUT3(n4_to_1_mux_3_output),
    .INPUT4(n4_to_1_mux_4_output), .s0(s3), .s1(s2), .OUTPUT(\output ));
endmodule

// least 4 bit
module shrink_to_4_bit (
  input  [15:0] _16_bit_input,
  output [3:0] _4_bit_output
);

  wire [15:4] and_1_out;

  assign {and_1_out, _4_bit_output} = _16_bit_input & 16'hf;  // AND_Gate and_1, 16 bits wide
endmodule

module subp8 (
  input  [15:0] A,
  input  [15:0] B,
  output [15:0] out_3,
  output Signed_Overflow
);

  wire sub_8bit_1_signed_overflow, sub_8bit_2_signed_overflow;
  wire [7:0] sub_8bit_1_output, sub_8bit_2_output;
  wire [15:0] bit_extender_1_out, bit_extender_2_out, shifter_1_out;

  SUB_8bit sub_8bit_1 (
    .input1(A[7:0]), .input2(B[7:0]), .Signed_Overflow(sub_8bit_1_signed_overflow),
    .\output (sub_8bit_1_output));
  SUB_8bit sub_8bit_2 (
    .input1(A[15:8]), .input2(B[15:8]), .Signed_Overflow(sub_8bit_2_signed_overflow),
    .\output (sub_8bit_2_output));
  or or_1 (Signed_Overflow, sub_8bit_2_signed_overflow, sub_8bit_1_signed_overflow);
  assign bit_extender_1_out = {{8{1'b0}}, sub_8bit_1_output};  // Bit_Extender bit_extender_1
  assign bit_extender_2_out = {{8{1'b0}}, sub_8bit_2_output};  // Bit_Extender bit_extender_2
  Shifter #(.width(16)) shifter_1 (.in(bit_extender_2_out), .\dist (4'b1000), .out(shifter_1_out));
  Adder #(.width(16)) adder_1 (.a(bit_extender_1_out), .b(shifter_1_out), .out(out_3));  // open: cin, cout
endmodule

module addp8 (
  input  [15:0] A,
  input  [15:0] B,
  output [15:0] out_3,
  output Unsigned_Overflow,
  output Signed_Overflow
);

  wire add_8bit_1_signed_overflow, add_8bit_1_unsigned_overflow, add_8bit_2_signed_overflow,
       add_8bit_2_unsigned_overflow;
  wire [7:0] add_8bit_1_output, add_8bit_2_output;
  wire [15:0] bit_extender_1_out, bit_extender_2_out, shifter_1_out;

  ADD_8bit add_8bit_1 (
    .input1(A[7:0]), .input2(B[7:0]), .Unsigned_Overflow(add_8bit_1_unsigned_overflow),
    .Signed_Overflow(add_8bit_1_signed_overflow), .\output (add_8bit_1_output));
  ADD_8bit add_8bit_2 (
    .input1(A[15:8]), .input2(B[15:8]), .Unsigned_Overflow(add_8bit_2_unsigned_overflow),
    .Signed_Overflow(add_8bit_2_signed_overflow), .\output (add_8bit_2_output));
  or or_1 (Unsigned_Overflow, add_8bit_1_unsigned_overflow, add_8bit_2_unsigned_overflow);
  or or_2 (Signed_Overflow, add_8bit_2_signed_overflow, add_8bit_1_signed_overflow);
  assign bit_extender_1_out = {{8{1'b0}}, add_8bit_1_output};  // Bit_Extender bit_extender_1
  assign bit_extender_2_out = {{8{1'b0}}, add_8bit_2_output};  // Bit_Extender bit_extender_2
  Shifter #(.width(16)) shifter_1 (.in(bit_extender_2_out), .\dist (4'b1000), .out(shifter_1_out));
  Adder #(.width(16)) adder_1 (.a(bit_extender_1_out), .b(shifter_1_out), .out(out_3));  // open: cin, cout
endmodule

module equals (
  input  [15:0] A,
  input  [15:0] B,
  output [15:0] out_3
);

  wire comparator_1_eq;

  Comparator #(.width(16)) comparator_1 (.a(A), .b(B), .eq(comparator_1_eq));  // open: gt, lt
  Multiplexer #(.width(16)) multiplexer_1 (.in0({16{1'b0}}), .in1(A), .out(out_3), .sel(comparator_1_eq));  // open: en
endmodule

module sltp8 (
  input  [15:0] A,
  input  [15:0] B,
  output [15:0] out_3
);

  wire comparator_1_lt, comparator_2_lt;
  wire [15:0] bit_extender_1_out, bit_extender_2_out, shifter_1_out;

  Comparator #(.mode("unsigned")) comparator_1 (.a(A[15:8]), .b(B[15:8]), .lt(comparator_1_lt));  // open: gt, eq
  assign bit_extender_1_out = {{15{1'b0}}, comparator_1_lt};  // Bit_Extender bit_extender_1
  Comparator #(.mode("unsigned")) comparator_2 (.a(A[7:0]), .b(B[7:0]), .lt(comparator_2_lt));  // open: gt, eq
  assign bit_extender_2_out = {{15{1'b0}}, comparator_2_lt};  // Bit_Extender bit_extender_2
  Shifter #(.width(16)) shifter_1 (.in(bit_extender_1_out), .\dist (4'b1000), .out(shifter_1_out));
  Adder #(.width(16)) adder_1 (.a(shifter_1_out), .b(bit_extender_2_out), .out(out_3));  // open: cin, cout
endmodule

module ADD_16bit (
  input  [15:0] input1,
  input  [15:0] input2,
  output [15:0] \output ,
  output Signed_Overflow,
  output Unsigned_Overflow
);

  wire comparator_1_eq, comparator_2_gt, comparator_2_lt;
  wire [15:0] multiplexer_1_out, shifter_1_out, shifter_2_out, shifter_3_out, xnor_1_out;

  Adder #(.width(16)) adder_1 (.a(input1), .b(input2), .out(\output ), .cout(Unsigned_Overflow));  // open: cin
  Shifter #(.width(16), .shift("lr")) shifter_1 (.in(input1), .\dist (4'b1111), .out(shifter_1_out));
  Shifter #(.width(16), .shift("lr")) shifter_2 (.in(input2), .\dist (4'b1111), .out(shifter_2_out));
  Shifter #(.width(16), .shift("lr")) shifter_3 (.in(\output ), .\dist (4'b1111), .out(shifter_3_out));
  assign xnor_1_out = ~(shifter_1_out ^ shifter_2_out);  // XNOR_Gate xnor_1, 16 bits wide
  Comparator #(.width(16)) comparator_1 (.a(xnor_1_out), .b({16{1'b1}}), .eq(comparator_1_eq));  // open: gt, lt
  Multiplexer #(.width(16), .enable("false")) multiplexer_1 (
    .in0(shifter_3_out), .in1(shifter_2_out), .out(multiplexer_1_out), .sel(comparator_1_eq));
  Comparator #(.width(16)) comparator_2 (
    .a(shifter_3_out), .b(multiplexer_1_out), .gt(comparator_2_gt), .lt(comparator_2_lt));  // open: eq
  or or_1 (Signed_Overflow, comparator_2_gt, comparator_2_lt);
endmodule

module ADD_8bit (
  input  [7:0] input1,
  input  [7:0] input2,
  output [7:0] \output ,
  output Signed_Overflow,
  output Unsigned_Overflow
);

  wire comparator_1_eq, comparator_2_gt, comparator_2_lt;
  wire [7:0] multiplexer_1_out, shifter_1_out, shifter_2_out, shifter_3_out, xnor_1_out;

  Adder adder_1 (.a(input1), .b(input2), .out(\output ), .cout(Unsigned_Overflow));  // open: cin
  Shifter #(.shift("lr")) shifter_1 (.in(input1), .\dist (3'b111), .out(shifter_1_out));
  Shifter #(.shift("lr")) shifter_2 (.in(input2), .\dist (3'b111), .out(shifter_2_out));
  Shifter #(.shift("lr")) shifter_3 (.in(\output ), .\dist (3'b111), .out(shifter_3_out));
  assign xnor_1_out = ~(shifter_1_out ^ shifter_2_out);  // XNOR_Gate xnor_1, 8 bits wide
  Comparator comparator_1 (.a(xnor_1_out), .b({8{1'b1}}), .eq(comparator_1_eq));  // open: gt, lt
  Multiplexer #(.width(8), .enable("false")) multiplexer_1 (
    .in0(shifter_3_out), .in1(shifter_2_out), .out(multiplexer_1_out), .sel(comparator_1_eq));
  Comparator comparator_2 (
    .a(shifter_3_out), .b(multiplexer_1_out), .gt(comparator_2_gt), .lt(comparator_2_lt));  // open: eq
  or or_1 (Signed_Overflow, comparator_2_gt, comparator_2_lt);
endmodule

module SUB_16bit (
  input  [15:0] input1,
  input  [15:0] input2,
  output [15:0] \output ,
  output Signed_Overflow
);

  wire comparator_1_eq, comparator_2_gt, comparator_2_lt;
  wire [15:0] multiplexer_1_out, shifter_1_out, shifter_2_out, shifter_3_out, xor_1_out;

  Subtractor #(.width(16)) subtractor_1 (.a(input1), .b(input2), .out(\output ));  // open: bin, bout
  Shifter #(.width(16), .shift("lr")) shifter_1 (.in(input1), .\dist (4'b1111), .out(shifter_1_out));
  Shifter #(.width(16), .shift("lr")) shifter_2 (.in(input2), .\dist (4'b1111), .out(shifter_2_out));
  Shifter #(.width(16), .shift("lr")) shifter_3 (.in(\output ), .\dist (4'b1111), .out(shifter_3_out));
  assign xor_1_out = shifter_1_out ^ shifter_2_out;  // XOR_Gate xor_1, 16 bits wide
  Comparator #(.width(16)) comparator_1 (.a(xor_1_out), .b(16'h1), .eq(comparator_1_eq));  // open: gt, lt
  Multiplexer #(.width(16), .enable("false")) multiplexer_1 (
    .in0(shifter_3_out), .in1(shifter_1_out), .out(multiplexer_1_out), .sel(comparator_1_eq));
  Comparator #(.width(16)) comparator_2 (
    .a(shifter_3_out), .b(multiplexer_1_out), .gt(comparator_2_gt), .lt(comparator_2_lt));  // open: eq
  or or_1 (Signed_Overflow, comparator_2_gt, comparator_2_lt);
endmodule

module SUB_8bit (
  input  [7:0] input1,
  input  [7:0] input2,
  output [7:0] \output ,
  output Signed_Overflow
);

  wire comparator_1_eq, comparator_2_gt, comparator_2_lt;
  wire [7:0] multiplexer_1_out, shifter_1_out, shifter_2_out, shifter_3_out, xor_1_out;

  Subtractor subtractor_1 (.a(input1), .b(input2), .out(\output ));  // open: bin, bout
  Shifter #(.shift("lr")) shifter_1 (.in(input1), .\dist (3'b111), .out(shifter_1_out));
  Shifter #(.shift("lr")) shifter_2 (.in(input2), .\dist (3'b111), .out(shifter_2_out));
  Shifter #(.shift("lr")) shifter_3 (.in(\output ), .\dist (3'b111), .out(shifter_3_out));
  assign xor_1_out = shifter_1_out ^ shifter_2_out;  // XOR_Gate xor_1, 8 bits wide
  Comparator comparator_1 (.a(xor_1_out), .b(8'h1), .eq(comparator_1_eq));  // open: gt, lt
  Multiplexer #(.width(8), .enable("false")) multiplexer_1 (
    .in0(shifter_3_out), .in1(shifter_1_out), .out(multiplexer_1_out), .sel(comparator_1_eq));
  Comparator comparator_2 (
    .a(shifter_3_out), .b(multiplexer_1_out), .gt(comparator_2_gt), .lt(comparator_2_lt));  // open: eq
  or or_1 (Signed_Overflow, comparator_2_gt, comparator_2_lt);
endmodule
